# Fritzing sketch circuito-porta (saved by Fritzing 0.9.3b)
breadboards: 1

parts:
  U2 = NodeMCU V1.0
  Componente2 = RFID-RC522-v3
  L2 = L298
  M2 = DC Motor
  LED1 = smd LED [color="Red (633nm)" package="0805 [SMD]"]
  LED2 = smd LED [color="Green (570nm)" package="0805 [SMD]"]
  R3 = Resistor [tolerance=±5% resistance=220 package=THT]
  R4 = Resistor [tolerance=±5% resistance=220 package=THT]
  J1 = Piezo Speaker
  S3 = Momentary Switch [package=tactile-pth]
  R5 = Resistor [tolerance=±5% resistance=220k package=THT]

nets:
  N1: U2.D1, Componente2.RST
  N2: U2.D2, J1.pin2
  N3: U2.D3, LED1.cathode
  N4: U2.D4, LED2.cathode
  3V3: U2.3V3, Componente2.3.3V, S3.1
  GND: U2.GND, Componente2.GND, L2.Gnd, R3.Pin_1, R4.Pin_1, J1.pin1, R5.Pin_0
  N5: U2.D5, Componente2.SCK
  N6: U2.D6, Componente2.MISO
  N7: U2.D7, Componente2.MOSI
  N8: U2.D8, Componente2.SDA
  N9: U2.A0, S3.3
  N10: L2.Motor_A_1, M2.pin_1
  N11: L2.Motor_A_2, M2.pin_2
  N12: LED1.anode, R4.Pin_0
  N13: LED2.anode, R3.Pin_0
  N14: S3.4, R5.Pin_1

notes:
  12V

custom parts:
  NodeMCU V1.0: ESP8266 based NodeMCU
  RFID-RC522-v3: A simple China made RFID-RC522 Reader (6x4 cm); do check the pin labels, as this is a MFRC522 based clone.
  L298: L298 module
