# Fritzing sketch esquematico_fritizing (saved by Fritzing 0.9.3b)
breadboards: 1

parts:
  U1 = NodeMCU V1.0
  LED1 = smd LED [color="Green (570nm)" package="0603 [SMD]"]  # not connected
  LED2 = smd LED [color="Green (570nm)" package="0603 [SMD]"]  # not connected
  LED3 = smd LED [color="Green (570nm)" package="0603 [SMD]"]  # not connected
  LED4 = smd LED [color="Green (570nm)" package="0603 [SMD]"]
  LED5 = smd LED [color="Green (570nm)" package="0603 [SMD]"]  # not connected
  LED7 = smd LED [color="Green (570nm)" package="0603 [SMD]"]
  LED8 = smd LED [color="Green (570nm)" package="0603 [SMD]"]
  LED9 = smd LED [color="Red (633nm)" package="0603 [SMD]"]
  U2 = 74HC595 [package="DIP16 [THT]"]
  R1 = Resistor [tolerance=±5% resistance=220 package="2512 [SMD]"]

nets:
  3V3: U1.3V3, U2.MR, U2.VCC
  GND: U1.GND, U2.GND, U2.OE, R1.Pin_1
  N1: U1.D8, U2.SH_CP
  N2: U1.RX, U2.DS
  N3: U1.TX, U2.ST_CP
  N4: LED4.anode, U2.Q6
  N5: LED7.cathode, LED7.anode
  N6: LED8.anode, U2.Q5
  N7: LED9.cathode, R1.Pin_0
  N8: LED9.anode, U2.Q7

custom parts:
  NodeMCU V1.0: ESP8266 based NodeMCU
